// Logisim project APUPlayer.circ as structural Verilog: 7 circuits, main circuit AUXDumper
module APUPlayer (
  input  nRES
);

  wire apu_m2__ext, apu_nirq_cpu, apu_nnmi_cpu, apu_phi0__cpu, apu_r_w__ext, apu_rdy__cpu, core_phi1,
       core_phi2, core_r_w, XTAL_out;
  wire [3:0] transp_latch_q_2;
  wire [7:0] apu_aux_a, apu_data_to_cpu, apu_db_out, core_db_out, wram_db_out;
  wire [11:0] transp_latch_q;
  wire [14:0] apu_aux_b;
  wire [15:0] apu_ab, core_addr;
  wire [23:0] dumper_addr;
  wire [31:0] dumper_data;

  Clock XTAL (.out(XTAL_out));
  _2A03_APU apu (
    .nRES_PIN(nRES), .RDY__CPU(apu_rdy__cpu), .R_W__CPU(core_r_w), .nIRQ_CPU(apu_nirq_cpu),
    .nNMI_CPU(apu_nnmi_cpu), .nNMI_PIN(1'b1), .R_W__EXT(apu_r_w__ext), .DBG__EXT(1'b0),
    .M2__EXT(apu_m2__ext), .PHI0__CPU(apu_phi0__cpu), .nIRQ_PIN(1'b1), .Data_to_CPU(apu_data_to_cpu),
    .Data_from_CPU(core_db_out), .AUX_A(apu_aux_a), .AUX_B(apu_aux_b), .CPU_Ax(core_addr), .AB(apu_ab),
    .DB_in(wram_db_out), .DB_out(apu_db_out), .PHI1_FromCore(core_phi1), .PHI2_FromCore(core_phi2),
    .CLK(XTAL_out));  // open: OUT0, OUT1, OUT2, nIN0, nIN1
  WRAM wram (
    .M2(apu_m2__ext), .Addr(apu_ab), .DB_in(apu_db_out), .R_W(apu_r_w__ext), .nRES(nRES), .DB_out(wram_db_out));
  Fake6502 core (
    .PHI0(apu_phi0__cpu), .RDY(apu_rdy__cpu), .SO(1'b1), .nNMI(apu_nnmi_cpu), .nIRQ(apu_nirq_cpu),
    .nRES(nRES), .DB_in(apu_data_to_cpu), .PHI1(core_phi1), .PHI2(core_phi2), .R_W(core_r_w),
    .Addr(core_addr), .DB_out(core_db_out));  // open: SYNC
  AUXDumper dumper (.PHI1(core_phi1), .AUX({1'b0, apu_aux_b, apu_aux_a}), .Addr(dumper_addr), .Data(dumper_data));
  Hex_Digit_Display hex_digit_display_1 (.value(transp_latch_q_2));  // open: dp
  Register #(.width(16), .trigger("high")) transp_latch (
    .D(core_addr), .en(core_addr[14]), .Q({transp_latch_q_2, transp_latch_q}), .clk(core_phi2));  // open: clr
  Hex_Digit_Display hex_digit_display_2 (.value(transp_latch_q[7:4]));  // open: dp
  Hex_Digit_Display hex_digit_display_3 (.value(transp_latch_q[11:8]));  // open: dp
  Hex_Digit_Display hex_digit_display_4 (.value(transp_latch_q[3:0]));  // open: dp
  RAM #(.addrWidth(24), .dataWidth(32), .bus("asynch")) ram_1 (
    .addr(dumper_addr), .data(dumper_data), .sel(1'b1), .ld(1'b0), .clr(1'b0));

  // Notes on the sheet:
  //   N.C.
  //   Load regdump here
  //   Last APU Register
  //   Taram-param-pam. Pam! Peep, peep, peep. Pipipipip, pip, pibibip
endmodule

module AUXDumper (
  input  PHI1,
  input  [23:0] AUX,
  output [23:0] Addr,
  output [31:0] Data
);

  wire adder_1_p3, counter_2_q, counter_3_q;
  wire [31:0] aux_a_1_a, aux_b_1_a;

  AUX_A aux_a_1 (.d(AUX[7:0]), .a(aux_a_1_a));
  AUX_B aux_b_1 (.d(AUX[23:8]), .a(aux_b_1_a));
  Counter #(.width(23), .max('h7fffff)) counter_1 (.Q(Addr[23:1]), .clk(PHI1));  // open: load, D, count, carry, clr
  Counter #(.width(1), .max('h1)) counter_2 (.Q(counter_2_q), .clk(PHI1));  // open: load, D, count, carry, clr
  Counter #(.width(1), .max('h1), .trigger("falling")) counter_3 (
    .Q(counter_3_q), .clk(PHI1));  // open: load, D, count, carry, clr
  // Adder adder_1: pin names not known; wires that end beside it: aux_a_1_a, aux_b_1_a, adder_1_p3
  // Divider divider_1: pin names not known; wires that end beside it: adder_1_p3, 32'h40000000, Data
  xnor xnor_1 (Addr[0], counter_2_q, counter_3_q);

  // Notes on the sheet:
  //   a + b
  //   The invention of the org to make the ADDR tick EVERY half cycle.
  //    : 2
  //   normalized samples in range [0.0f; 1.0f]
endmodule

module AUX_A (
  input  [7:0] d,
  output [31:0] a
);

  ROM #(.dataWidth(32)) rom_1 (.addr(d), .data(a), .sel(1'b1));

  // Notes on the sheet:
  //   0...255
  //   contents of rom_1 (hex, n*v repeats v):
  //   bf7f4884 bf6daae3 bf5b6db7 bf49484e bf373a7a bf25440d bf1364d9 bf019cb2 bedfd6d6 bebca1af be99999a
  //   be6d7c7d be281e91 bdc6318c bcf353a5 3d17b426 bf6daae3 bf5b6db7 bf49484e bf373a7a bf25440d bf1364d9
  //   bf019cb2 bedfd6d6 bebca1af be99999a be6d7c7d be281e91 bdc6318c bcf353a5 3d17b426 3dd3dcb1 bf5b6db7
  //   bf49484e bf373a7a bf25440d bf1364d9 bf019cb2 bedfd6d6 bebca1af be99999a be6d7c7d be281e91 bdc6318c
  //   bcf353a5 3d17b426 3dd3dcb1 3e2d9a1a bf49484e bf373a7a bf25440d bf1364d9 bf019cb2 bedfd6d6 bebca1af
  //   be99999a be6d7c7d be281e91 bdc6318c bcf353a5 3d17b426 3dd3dcb1 3e2d9a1a 3e70f0f1 bf373a7a bf25440d
  //   bf1364d9 bf019cb2 bedfd6d6 bebca1af be99999a be6d7c7d be281e91 bdc6318c bcf353a5 3d17b426 3dd3dcb1
  //   3e2d9a1a 3e70f0f1 3e99f9be bf25440d bf1364d9 bf019cb2 bedfd6d6 bebca1af be99999a be6d7c7d be281e91
  //   bdc6318c bcf353a5 3d17b426 3dd3dcb1 3e2d9a1a 3e70f0f1 3e99f9be 3ebb512c bf1364d9 bf019cb2 bedfd6d6
  //   bebca1af be99999a be6d7c7d be281e91 bdc6318c bcf353a5 3d17b426 3dd3dcb1 3e2d9a1a 3e70f0f1 3e99f9be
  //   3ebb512c 3edc7f11 bf019cb2 bedfd6d6 bebca1af be99999a be6d7c7d be281e91 bdc6318c bcf353a5 3d17b426
  //   3dd3dcb1 3e2d9a1a 3e70f0f1 3e99f9be 3ebb512c 3edc7f11 3efd83ba bedfd6d6 bebca1af be99999a be6d7c7d
  //   be281e91 bdc6318c bcf353a5 3d17b426 3dd3dcb1 3e2d9a1a 3e70f0f1 3e99f9be 3ebb512c 3edc7f11 3efd83ba
  //   3f0f2fbb bebca1af be99999a be6d7c7d be281e91 bdc6318c bcf353a5 3d17b426 3dd3dcb1 3e2d9a1a 3e70f0f1
  //   3e99f9be 3ebb512c 3edc7f11 3efd83ba 3f0f2fbb 3f1f8946 be99999a be6d7c7d be281e91 bdc6318c bcf353a5
  //   3d17b426 3dd3dcb1 3e2d9a1a 3e70f0f1 3e99f9be 3ebb512c 3edc7f11 3efd83ba 3f0f2fbb 3f1f8946 3f2fcea7
  //   be6d7c7d be281e91 bdc6318c bcf353a5 3d17b426 3dd3dcb1 3e2d9a1a 3e70f0f1 3e99f9be 3ebb512c 3edc7f11
  //   3efd83ba 3f0f2fbb 3f1f8946 3f2fcea7 3f400000 be281e91 bdc6318c bcf353a5 3d17b426 3dd3dcb1 3e2d9a1a
  //   3e70f0f1 3e99f9be 3ebb512c 3edc7f11 3efd83ba 3f0f2fbb 3f1f8946 3f2fcea7 3f400000 3f501d78 bdc6318c
  //   bcf353a5 3d17b426 3dd3dcb1 3e2d9a1a 3e70f0f1 3e99f9be 3ebb512c 3edc7f11 3efd83ba 3f0f2fbb 3f1f8946
  //   3f2fcea7 3f400000 3f501d78 3f602732 bcf353a5 3d17b426 3dd3dcb1 3e2d9a1a 3e70f0f1 3e99f9be 3ebb512c
  //   3edc7f11 3efd83ba 3f0f2fbb 3f1f8946 3f2fcea7 3f400000 3f501d78 3f602732 3f701d54 3d17b426 3dd3dcb1
  //   3e2d9a1a 3e70f0f1 3e99f9be 3ebb512c 3edc7f11 3efd83ba 3f0f2fbb 3f1f8946 3f2fcea7 3f400000 3f501d78
  //   3f602732 3f701d54 3f800000
endmodule

module AUX_B (
  input  [15:0] d,
  output [31:0] a
);

  ROM #(.addrWidth(15), .dataWidth(32)) rom_1 (.addr(d[14:0]), .data(a), .sel(1'b1));

  // Notes on the sheet:
  //   0...32767
  //   contents of rom_1 (hex, n*v repeats v):
  //   bf7fc3c9 bf73ff85 bf681e3b bf5c5ba9 bf50b759 bf4530d7 bf39c7b1 bf2e7b76 bf234bbb bf183812 bf0d4014
  //   bf026359 beef42f8 bed9f434 bec4d9a2 beaff284 bf79fbd5 bf6e0b01 bf623922 bf5685c0 bf4af066 bf3f78a0
  //   bf341dfd bf28e00f bf1dbe6b bf12b8a5 bf07ce55 bef9fe2b bee49504 becf6071 beba5fb1 bea59206 bf73ff85
  //   bf681e3b bf5c5ba9 bf50b759 bf4530d7 bf39c7b1 bf2e7b76 bf234bbb bf183812 bf0d4014 bf026359 beef42f8
  //   bed9f434 bec4d9a2 beaff284 be9b3e1f bf6e0b01 bf623922 bf5685c0 bf4af066 bf3f78a0 bf341dfd bf28e00f
  //   bf1dbe6b bf12b8a5 bf07ce55 bef9fe2b bee49504 becf6071 beba5fb1 bea59206 be90f6b9 bf681e3b bf5c5ba9
  //   bf50b759 bf4530d7 bf39c7b1 bf2e7b76 bf234bbb bf183812 bf0d4014 bf026359 beef42f8 bed9f434 bec4d9a2
  //   beaff284 be9b3e1f be86bbbb bf623922 bf5685c0 bf4af066 bf3f78a0 bf341dfd bf28e00f bf1dbe6b bf12b8a5
  //   bf07ce55 bef9fe2b bee49504 becf6071 beba5fb1 bea59206 be90f6b9 be791a22 bf5c5ba9 bf50b759 bf4530d7
  //   bf39c7b1 bf2e7b76 bf234bbb bf183812 bf0d4014 bf026359 beef42f8 bed9f434 bec4d9a2 beaff284 be9b3e1f
  //   be86bbbb be64d548 bf5685c0 bf4af066 bf3f78a0 bf341dfd bf28e00f bf1dbe6b bf12b8a5 bf07ce55 bef9fe2b
  //   bee49504 becf6071 beba5fb1 bea59206 be90f6b9 be791a22 be50a8bb bf50b759 bf4530d7 bf39c7b1 bf2e7b76
  //   bf234bbb bf183812 bf0d4014 bf026359 beef42f8 bed9f434 bec4d9a2 beaff284 be9b3e1f be86bbbb be64d548
  //   be3c9450 bf4af066 bf3f78a0 bf341dfd bf28e00f bf1dbe6b bf12b8a5 bf07ce55 bef9fe2b bee49504 becf6071
  //   beba5fb1 bea59206 be90f6b9 be791a22 be50a8bb be2897dd bf4530d7 bf39c7b1 bf2e7b76 bf234bbb bf183812
  //   bf0d4014 bf026359 beef42f8 bed9f434 bec4d9a2 beaff284 be9b3e1f be86bbbb be64d548 be3c9450 be14b335
  //   bf3f78a0 bf341dfd bf28e00f bf1dbe6b bf12b8a5 bf07ce55 bef9fe2b bee49504 becf6071 beba5fb1 bea59206
  //   be90f6b9 be791a22 be50a8bb be2897dd be00e630 bf39c7b1 bf2e7b76 bf234bbb bf183812 bf0d4014 bf026359
  //   beef42f8 bed9f434 bec4d9a2 beaff284 be9b3e1f be86bbbb be64d548 be3c9450 be14b335 bdda6143 bf341dfd
  //   bf28e00f bf1dbe6b bf12b8a5 bf07ce55 bef9fe2b bee49504 becf6071 beba5fb1 bea59206 be90f6b9 be791a22
  //   be50a8bb be2897dd be00e630 bdb324c3 bf2e7b76 bf234bbb bf183812 bf0d4014 bf026359 beef42f8 bed9f434
  //   bec4d9a2 beaff284 be9b3e1f be86bbbb be64d548 be3c9450 be14b335 bdda6143 bd8c168d bf28e00f bf1dbe6b
  //   bf12b8a5 bf07ce55 bef9fe2b bee49504 becf6071 beba5fb1 bea59206 be90f6b9 be791a22 be50a8bb be2897dd
  //   be00e630 bdb324c3 bd4a6c9e bf7cfcee bf71044a bf652aba bf596fc4 bf4dd2f2 bf4253d1 bf36f1f0 bf2bace0
  //   bf208433 bf15777f bf0a865b beff60c2 bee9ea58 bed4a8b2 bebf9b0f beaac0b1 bf76fcb2 bf6b13a7 bf5f4973
  //   bf539d9e bf480fb3 bf3c9f40 bf314bd5 bf261504 bf1afa60 bf0ffb81 bf0517ff bef49ee8 bedf42f9 beca1b6c
  //   beb52783 bea06681 bf71044a bf652aba bf596fc4 bf4dd2f2 bf4253d1 bf36f1f0 bf2bace0 bf208433 bf15777f
  //   bf0a865b beff60c2 bee9ea58 bed4a8b2 bebf9b0f beaac0b1 be9618dd bf6b13a7 bf5f4973 bf539d9e bf480fb3
  //   bf3c9f40 bf314bd5 bf261504 bf1afa60 bf0ffb81 bf0517ff bef49ee8 bedf42f9 beca1b6c beb52783 bea06681
  //   be8bd7ae bf652aba bf596fc4 bf4dd2f2 bf4253d1 bf36f1f0 bf2bace0 bf208433 bf15777f bf0a865b beff60c2
  //   bee9ea58 bed4a8b2 bebf9b0f beaac0b1 be9618dd be81a2dd bf5f4973 bf539d9e bf480fb3 bf3c9f40 bf314bd5
  //   bf261504 bf1afa60 bf0ffb81 bf0517ff bef49ee8 bedf42f9 beca1b6c beb52783 bea06681 be8bd7ae be6ef4a9
  //   bf596fc4 bf4dd2f2 bf4253d1 bf36f1f0 bf2bace0 bf208433 bf15777f bf0a865b beff60c2 bee9ea58 bed4a8b2
  //   bebf9b0f beaac0b1 be9618dd be81a2dd be5abbfa bf539d9e bf480fb3 bf3c9f40 bf314bd5 bf261504 bf1afa60
  //   bf0ffb81 bf0517ff bef49ee8 bedf42f9 beca1b6c beb52783 bea06681 be8bd7ae be6ef4a9 be469b84 bf4dd2f2
  //   bf4253d1 bf36f1f0 bf2bace0 bf208433 bf15777f bf0a865b beff60c2 bee9ea58 bed4a8b2 bebf9b0f beaac0b1
  //   be9618dd be81a2dd be5abbfa be32931a bf480fb3 bf3c9f40 bf314bd5 bf261504 bf1afa60 bf0ffb81 bf0517ff
  //   bef49ee8 bedf42f9 beca1b6c beb52783 bea06681 be8bd7ae be6ef4a9 be469b84 be1ea292 bf4253d1 bf36f1f0
  //   bf2bace0 bf208433 bf15777f bf0a865b beff60c2 bee9ea58 bed4a8b2 bebf9b0f beaac0b1 be9618dd be81a2dd
  //   be5abbfa be32931a be0ac9c1 bf3c9f40 bf314bd5 bf261504 bf1afa60 bf0ffb81 bf0517ff bef49ee8 bedf42f9
  //   beca1b6c beb52783 bea06681 be8bd7ae be6e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
endmodule

module Fake6502 (
  input  PHI0,
  input  RDY,
  input  SO,
  input  nNMI,
  input  nIRQ,
  input  nRES,
  input  [7:0] DB_in,
  output PHI1,
  output PHI2,
  output R_W,
  output SYNC,
  output [15:0] Addr,
  output [7:0] DB_out
);

  wire [23:0] redump_redump_addr;
  wire [31:0] rom_1_data;

  ROM #(.addrWidth(24), .dataWidth(32)) rom_1 (.addr(redump_redump_addr), .data(rom_1_data), .sel(1'b1));
  RegDumpProcessor redump (
    .PHI0(PHI0), .regdump_data(rom_1_data), .Core_R_W(R_W), .Core_AB(Addr), .Core_DB(DB_out),
    .redump_addr(redump_redump_addr));
  not not_1 (PHI1, PHI0);

  assign PHI2 = PHI0;
  assign SYNC = 1'b0;

  // Notes on the sheet:
  //   N.C.
  //   N.C.
  //   N.C.
  //   Load regdump here
  //   contents of rom_1 (hex, n*v repeats v):
  //   4 11 d 0 4 4 4 8 4 c 6 f15 15 f15 78 714 e8a4 714 27e 116 6 16 22a 116 6 16 3cd e08 1f c40a c 90b cc
  //   8104 16 805 11 c406 c 907 cc 8100 16 801 11 e102 c 803 88 11 d 0 4 4 4 8 4 c 6 f15 6904 714 2c3 116
  //   6 16 22a 116 6 16 6f5b 714 2c3 116 6 16 22a 116 6 16 6f5b 714 2c3 116 6 16 22a 116 6 16 6f5e 714 2c2
  //   116 6 16 22a 116 6 16 6f5b 714 2c3 116 6 16 22a 116 6 16 6f5b 714 2c3 116 6 16 22a 116 6 16 6f5e 714
  //   2c2 116 6 16 22a 116 6 16 2cc e08 1f c40a c 90b 9f 8104 16 805 11 e106 c 807 9f 8100 16 801 11 7002
  //   c 803 6ac1 714 2c2 116 6 16 22a 116 6 16 6f5b 714 2c3 116 6 16 22a 116 6 16 6f5b 714 2c3 116 6 16
  //   22a 116 6 16 6f5e 714 2c2 116 6 16 22a 116 6 16 6f5b 714 2c3 116 6 16 22a 116 6 16 6f5b 714 2c3 116
  //   6 16 22a 116 6 16 6f5b 714 2c3 116 6 16 22a 116 6 16 2cc e08 1f c40a c 90b 9f 8104 16 805 11 7006 c
  //   807 9f 8100 16 801 11 3702 c 803 6ac1 714 2c2 116 6 16 22a 116 6 16 6f5b 714 2c3 116 6 16 22a 116 6
  //   16 6f5e 714 2c2 116 6 16 22a 116 6 16 6f5b 714 2c3 116 6 16 22a 116 6 16 6f5b 714 2c3 116 6 16 22a
  //   116 6 16 6f5e 714 2c2 116 6 16 22a 116 6 16 6f5b 714 2c3 116 6 16 22a 116 6 16 2cc e08 1f c40a c 90b
  //   9f 8104 16 805 11 e106 c 807 9f 8100 16 801 11 7002 c 803 6ac1 714 2c2 116 6 16 22a 116 6 16 6f5b
  //   714 2c3 116 6 16 22a 116 6 16 6f5e 714 2c2 116 6 16 22a 116 6 16 6f5b 714 2c3 116 6 16 22a 116 6 16
  //   6f5b 714 2c3 116 6 16 22a 116 6 16 6f5e 714 2c2 116 6 16 22a 116 6 16 6f5b 714 2c3 116 6 16 22a 116
  //   6 16 37d 8104 16 805 11 bd06 c 807 9f 8100 16 801 11 5e02 c 803 6ad9 714 2c3 116 6 16 22a 116 6 16
  //   6f5b 714 2c3 116 6 16 22a 116 6 16 6f5e 714 2c2 116 6 16 22a 116 6 16 6f5b 714 2c3 116 6 16 22a 116
  //   6 16 6f5b 714 2c3 116 6 16 22a 116 6 16 6f5b 714 2c3 116 6 16 22a 116 6 16 6f5b 714 2c3 116 6 16 22a
  //   116 6 16 2e2 8104 16 805 11 b206 c 807 9f 8100 16 801 11 5802 c 803 6b75 714 2c2 116 6 16 22a 116 6
  //   16 6f5e 714 2c2 116 6 16 22a 116 6 16 6f5b 714 2c3 116 6 16 22a 116 6 16 6f5b 714 2c3 116 6 16 22a
  //   116 6 16 6f5e 714 2c2 116 6 16 22a 116 6 16 6f5b 714 2c3 116 6 16 22a 116 6 16 6f5b 714 2c3 116 6 16
  //   22a 116 6 16 2e2 8104 16 805 11 e106 c 807 9f 8100 16 801 11 7002 c 803 6b75 714 2c2 116 6 16 22a
  //   116 6 16 6f5e 714 2c2 116 6 16 22a 116 6 16 6f5b 714 2c3 116 6 16 22a 116 6 16 6f5b 714 2c3 116 6 16
  //   22a 116 6 16 6f5e 714 2c2 116 6 16 22a 116 6 16 6f5b 714 2c3 116 6 16 22a 116 6 16 6f5b 714 2c3 116
  //   6 16 22a 116 6 16 2e2 8104 16 805 11 fd06 c 807 9f 8100 16 801 11 7e02 c 803 6b75 714 2c2 116 6 16
  //   22a 116 6 16 6f5e 714 2c2 116 6 16 22a 116 6 16 6f5b 714 2c3 116 6 16 22a 116 6 16 6f5b 714 2c3 116
  //   6 16 22a 116 6 16 6f5b 714 2c3 116 6 16 22a 116 6 16 6f5b 714 2c3 116 6 16 22a 116 6 16 6f5e 714 2c2
  //   116 6 16 22a 116 6 16 2f9 e08 1f c40a c 90b 9f 8104 16 805 11 c406 c 907 9f 8100 16 801 11 e102 c
  //   803 6a94 714 2c2 116 6 16 22a 116 6 16 6f5b 714 2c3 116 6 16 22a 116 6 16 6f5e 714 2c2 116 6 16 22a
  //   116 6 16 6f5b 714 2c3 116 6 16 22a 116 6 16 6f5b 714 2c3 116 6 16 22a 116 6 16 6f5b 714 2c3 116 6 16
  //   22a 116 6 16 6f5b 714 2c3 116 6 16 22a 116 6 16 2cc e08 1f c40a c 90b 9f 8104 16 805 11 e106 c 807
  //   9f 8100 16 801 11 7002 c 803 6ac1 714 2c2 116 6 16 22a 116 6 16 6f5e 714 2c2 116 6 16 22a 116 6 16
  //   6f5b 714 2c3 116 6 16 22a 116 6 16 6f5b 714 2c3 116 6 16 22a 116 6 16 6f5e 714 2c2 116 6 16 22a 116
  //   6 16 6f5b 714 2c3 116 6 16 22a 116 6 16 6f5b 714 2c3 116 6 16 22a 116 6 16 2cc e08 1f c40a c 90b 9f
  //   8104 16 805 11 7006 c 807 9f 8100 16 801 11 3702 c 803 6ac1 714 2c2 116 6 16 22a 116 6 16 6f5e 714
  //   2c2 116 6 16 22a 116 6 16 6f5b 714 2c3 116 6 16 22a 116 6 16 6f5b 714 2c3 116 6 16 22a 116 6 16 6f5e
  //   714 2c2 116 6 16 22a 116 6 16 6f5b 714 2c3 116 6 16 22a 116 6 16 6f5b 714 2c3 116 6 16 22a 116 6 16
  //   2cc e08 1f c40a c 90b 9f 8104 16 805 11 e106 c 807 9f 8100 16 801 11 7002 c 803 6ac1 714 2c2 116 6
  //   16 22a 116 6 16 6f5e 714 2c2 116 6 16 22a 116 6 16 6f5b 714 2c3 116 6 16 22a 116 6 16 6f5b 714 2c3
  //   116 6 16 22a 116 6 16 6f5b 714 2c3 116 6 16 22a 116 6 16 6f5b 714 2c3 116 6 16 22a 116 6 16 6f5e 714
  //   2c2 116 6 16 22a 116 6 16 37d 8104 16 805 11 bd06 c 807 9f 8100 16 801 11 5e02 c 803 6ad9 714 2c3
  //   116 6 16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
endmodule

module WRAM (
  input  M2,
  input  [15:0] Addr,
  input  [7:0] DB_in,
  input  R_W,
  input  nRES,
  output [7:0] DB_out
);

  wire nor_1_out, not_1_out, not_2_out;

  not not_1 (not_1_out, nRES);
  nor nor_1 (nor_1_out, Addr[11], Addr[12], Addr[13], Addr[14], Addr[15]);
  not not_2 (not_2_out, R_W);
  RAM #(.addrWidth(11), .bus("separate")) ram_1 (
    .addr(Addr[10:0]), .din(DB_in), .data(DB_out), .str(not_2_out), .sel(nor_1_out), .clk(M2), .ld(R_W),
    .clr(not_1_out));
endmodule

module RegDumpProcessor (
  input  PHI0,
  input  [31:0] regdump_data,
  output Core_R_W,
  output [15:0] Core_AB,
  output [7:0] Core_DB,
  output [23:0] redump_addr
);

  wire and_1_out, and_2_out, cnt_ovf_reg_q, comparator_1_eq, comparator_2_gt, multiplexer_1_out,
       multiplexer_2_out, not_1_out, or_1_out;
  wire [7:0] regop_word_q_2, undriven;
  wire [15:0] or_2_out;
  wire [31:0] delta_pclk_word_q, phi_dec_cnt_q, regop_word_q;

  Multiplexer #(.enable("false")) multiplexer_1 (.in0(1'b1), .in1(1'b1), .out(multiplexer_1_out), .sel(cnt_ovf_reg_q));
  Multiplexer #(.enable("false")) multiplexer_2 (.in0(1'b1), .in1(1'b0), .out(multiplexer_2_out), .sel(cnt_ovf_reg_q));
  Register #(.width(32)) delta_pclk_word (
    .D(regdump_data), .Q(delta_pclk_word_q), .clk(cnt_ovf_reg_q));  // open: en, clr
  Counter #(.width(32), .max('hffffffff), .ongoal("stay")) phi_dec_cnt (
    .load(multiplexer_1_out), .D(delta_pclk_word_q), .count(multiplexer_2_out), .Q(phi_dec_cnt_q), .clk(PHI0));  // open: carry, clr
  Register #(.width(32)) regop_word (
    .D(regdump_data), .Q({regop_word_q[31:16], regop_word_q_2, regop_word_q[7:0]}), .clk(and_1_out));  // open: en, clr
  Comparator #(.width(32)) comparator_1 (.a(phi_dec_cnt_q), .b({32{1'b0}}), .eq(comparator_1_eq));  // open: gt, lt
  Comparator #(.width(32)) comparator_2 (.a(delta_pclk_word_q), .b({32{1'b0}}), .gt(comparator_2_gt));  // open: eq, lt
  Register #(.width(1)) cnt_ovf_reg (.D(comparator_1_eq), .Q(cnt_ovf_reg_q), .clk(PHI0));  // open: en, clr
  and and_1 (and_1_out, PHI0, comparator_2_gt, comparator_1_eq, ~cnt_ovf_reg_q);  // AND_Gate
  or or_1 (or_1_out, and_1_out, cnt_ovf_reg_q);
  assign or_2_out = 16'h4000 | {{11{1'b0}}, regop_word_q[4:0]};  // OR_Gate or_2, 16 bits wide
  not not_1 (not_1_out, regop_word_q[7]);
  Multiplexer #(.enable("false")) multiplexer_3 (.in0(1'b1), .in1(regop_word_q[7]), .out(Core_R_W), .sel(and_1_out));
  Multiplexer #(.width(16), .enable("false")) multiplexer_4 (
    .in0({16{1'b0}}), .in1(or_2_out), .out(Core_AB), .sel(and_1_out));
  Multiplexer #(.width(8), .enable("false")) multiplexer_5 (
    .in0(undriven), .in1(regop_word_q_2), .out(Core_DB), .sel(and_2_out));
  and and_2 (and_2_out, and_1_out, not_1_out);
  Counter #(.width(24), .max('hffffff), .ongoal("stay"), .trigger("falling")) addr_cnt (
    .load(1'b0), .count(1'b1), .Q(redump_addr), .clk(or_1_out));  // open: D, carry, clr

  // Notes on the sheet:
  //   https://github.com/emu-russia/breaknes/blob/main/BreaksAPU/NSFPlayerInterop/RegDumpProcessor.cpp
  //   Load/Decrement Setup (1: Load; 0: Decrement)
  //   Do RegOp
  //   Load PHI Counter
  //   RegOp Setup
  //   Reg Index (0-0x1f)
  //   Reg Address
  //   Value (if write)
  //   1: Read register
  //   z
  //   Default: Read address 0x0000
  //   1: RegOp + Write
  //   Falling edge
endmodule
