// Logisim project PPUPlayer.circ as structural Verilog: 6 circuits, main circuit PPUPlayer_All
module PPUPlayer_All (
  input  nRES
);

  wire CLK_out, n2c02_ntsc_1_ale, n2c02_ntsc_1_nrd, n2c02_ntsc_1_nwr, not_1_out, not_2_out,
       nrom_cartridge_1_nvram_cs, pull_resistor_1_node;
  wire [5:0] n2c02_ntsc_1_pa8;
  wire [7:0] ls373_1_val_out, n2c02_ntsc_1_pa0, n2c02_ntsc_1_pd0_w, nrom_cartridge_1_ppudata_out;
  wire [10:0] n2c02_ntsc_1_vout;
  wire [10:10] nrom_cartridge_1_vram_a10;

  Clock CLK (.out(CLK_out));
  Pull_Resistor #(.pull(1)) pull_resistor_1 (.node(pull_resistor_1_node));
  _2C02_NTSC u_2c02_ntsc_1 (
    .VOUT(n2c02_ntsc_1_vout), .nRES(nRES), .nINT(pull_resistor_1_node), .RS2(1'b0), .RS1(1'b0), .RS0(1'b0),
    .R_W(1'b0), .D7(1'b0), .D6(1'b0), .D5(1'b0), .D4(1'b0), .D3(1'b0), .D2(1'b0), .D1(1'b0), .D0(1'b0),
    .nRD(n2c02_ntsc_1_nrd), .nWR(n2c02_ntsc_1_nwr), .PA13(n2c02_ntsc_1_pa8[5]), .PA12(n2c02_ntsc_1_pa8[4]),
    .PA11(n2c02_ntsc_1_pa8[3]), .PA10(n2c02_ntsc_1_pa8[2]), .PA9(n2c02_ntsc_1_pa8[1]),
    .PA8(n2c02_ntsc_1_pa8[0]), .PA7(n2c02_ntsc_1_pa0[7]), .PA6(n2c02_ntsc_1_pa0[6]),
    .PA5(n2c02_ntsc_1_pa0[5]), .PA4(n2c02_ntsc_1_pa0[4]), .PA3(n2c02_ntsc_1_pa0[3]),
    .PA2(n2c02_ntsc_1_pa0[2]), .PA1(n2c02_ntsc_1_pa0[1]), .PA0(n2c02_ntsc_1_pa0[0]), .ALE(n2c02_ntsc_1_ale),
    .PD7(nrom_cartridge_1_ppudata_out[7]), .PD6(nrom_cartridge_1_ppudata_out[6]),
    .PD5(nrom_cartridge_1_ppudata_out[5]), .PD4(nrom_cartridge_1_ppudata_out[4]),
    .PD3(nrom_cartridge_1_ppudata_out[3]), .PD2(nrom_cartridge_1_ppudata_out[2]),
    .PD1(nrom_cartridge_1_ppudata_out[1]), .PD0(nrom_cartridge_1_ppudata_out[0]),
    .PD7_W(n2c02_ntsc_1_pd0_w[7]), .PD6_W(n2c02_ntsc_1_pd0_w[6]), .PD5_W(n2c02_ntsc_1_pd0_w[5]),
    .PD4_W(n2c02_ntsc_1_pd0_w[4]), .PD3_W(n2c02_ntsc_1_pd0_w[3]), .PD2_W(n2c02_ntsc_1_pd0_w[2]),
    .PD1_W(n2c02_ntsc_1_pd0_w[1]), .PD0_W(n2c02_ntsc_1_pd0_w[0]), .EXT0(1'b0), .EXT1(1'b0), .EXT2(1'b0),
    .EXT3(1'b0), .CLK(CLK_out), .nDBE(1'b1), .DbgRenderEnable(1'b1));  // open: D7_2, D6_2, D5_2, D4_2, D3_2, D2_2, D1_2, D0_2, EXT0_2, EXT1_2, EXT2_2, EXT3_2, RAW_OUT
  not not_1 (not_1_out, pull_resistor_1_node);
  LED led_1 (.in(not_1_out));
  VideoDumper videodumper_1 (.CLK(CLK_out), .VideoIn(n2c02_ntsc_1_vout));
  LS373 ls373_1 (.LE(n2c02_ntsc_1_ale), .nOE(1'b0), .val_in(n2c02_ntsc_1_pa0), .val_out(ls373_1_val_out));
  NROM_Cartridge nrom_cartridge_1 (
    .PPUData_In(n2c02_ntsc_1_pd0_w), .nRD(n2c02_ntsc_1_nrd), .nWR(n2c02_ntsc_1_nwr),
    .PPUAddr({n2c02_ntsc_1_pa8, ls373_1_val_out}), .nPA13(not_2_out),
    .PPUData_Out(nrom_cartridge_1_ppudata_out), .nVRAM_CS(nrom_cartridge_1_nvram_cs),
    .VRAM_A10(nrom_cartridge_1_vram_a10[10]), .V_Mirroring(1'b1));
  not not_2 (not_2_out, n2c02_ntsc_1_pa8[5]);
  SRAM sram_1 (
    .nCS(nrom_cartridge_1_nvram_cs), .nWE(n2c02_ntsc_1_nwr), .nOE(n2c02_ntsc_1_nrd),
    .Addr({nrom_cartridge_1_vram_a10[10], n2c02_ntsc_1_pa8[1:0], ls373_1_val_out}),
    .Data_In(n2c02_ntsc_1_pd0_w), .Data_Out(nrom_cartridge_1_ppudata_out));

  // Notes on the sheet:
  //   PA0-7
  //   PPU Data Out
  //   PPU Data In
endmodule

module PPUPlayer_NTSC (
  input  CLK,
  input  [31:0] RegData,
  output RS0,
  output RS1,
  output RS2,
  output R_W,
  output nRES,
  output [7:0] DB_Out,
  output nDBE,
  output [23:0] RegAddr,
  output DataLoad,
  output [31:0] Scan
);

  wire and_1_out, comparator_1_lt, comparator_2_eq, comparator_2_gt, comparator_3_eq, not_1_out, not_3_out,
       or_1_out;
  wire [1:0] pixel_clock_ntsc_1_pclk;
  wire [31:0] adder_1_out, counter_1_q, counter_2_q, demultiplexer_1_out0, demultiplexer_1_out1,
       register_1_q, register_2_q;
  wire [31:3] register_3_q;

  not not_1 (not_1_out, CLK);
  Counter #(.width(32), .max('hffffffff)) counter_1 (
    .count(not_1_out), .Q(counter_1_q), .clk(not_1_out));  // open: load, D, carry, clr
  Comparator #(.width(32)) comparator_1 (.a(counter_1_q), .b(32'h2), .lt(comparator_1_lt));  // open: gt, eq
  PIXEL_CLOCK_NTSC pixel_clock_ntsc_1 (
    .nCLK(not_1_out), .RES(comparator_1_lt), .PCLK(pixel_clock_ntsc_1_pclk));  // open: nPCLK, PCLK_2
  not not_2 (nRES, comparator_1_lt);
  Demultiplexer #(.width(32), .enable("false")) demultiplexer_1 (
    .out0(demultiplexer_1_out0), .out1(demultiplexer_1_out1), .in(register_1_q), .sel(RegAddr[2]));
  Register #(.width(32)) register_1 (.D(RegData), .en(DataLoad), .Q(register_1_q), .clk(CLK));  // open: clr
  Adder #(.width(32)) adder_1 (.a(counter_2_q), .b(demultiplexer_1_out0), .out(adder_1_out), .cin(1'b0));  // open: cout
  Counter #(.width(32), .max('hffffffff)) counter_2 (
    .count(pixel_clock_ntsc_1_pclk[1]), .Q(counter_2_q), .clk(pixel_clock_ntsc_1_pclk[1]));  // open: load, D, carry, clr
  Register #(.width(32)) register_2 (.D(adder_1_out), .en(DataLoad), .Q(register_2_q), .clk(CLK));  // open: clr
  and and_1 (and_1_out, comparator_2_eq, DataLoad);
  Comparator #(.width(32)) comparator_2 (
    .a(counter_2_q), .b(register_2_q), .gt(comparator_2_gt), .eq(comparator_2_eq));  // open: lt
  Counter #(.width(22), .max('h3fffff)) counter_3 (
    .count(and_1_out), .Q(RegAddr[23:2]), .clk(CLK));  // open: load, D, carry, clr
  Comparator #(.width(32)) comparator_3 (.a(counter_2_q), .b({32{1'b0}}), .eq(comparator_3_eq));  // open: gt, lt
  and and_2 (DataLoad, ~comparator_3_eq, or_1_out);  // AND_Gate
  or or_1 (or_1_out, comparator_2_gt, comparator_2_eq);
  not not_3 (not_3_out, DataLoad);
  Register #(.width(32)) register_3 (
    .D(demultiplexer_1_out1), .en(not_3_out),
    .Q({register_3_q[31:16], DB_Out, R_W, register_3_q[6:3], RS2, RS1, RS0}), .clk(CLK));  // open: clr
  not not_4 (nDBE, DataLoad);
  Divider #(.width(32)) divider_1 (.a(counter_2_q), .b(32'h155), .out(Scan));  // open: upper, rem

  assign RegAddr[1:0] = 2'b00;

  // Notes on the sheet:
  //   InputReg
  //   PCLK Counter
  //   NextPCLK
  //   Modulo +4
  //   OutputReg
  //   CPU I/F
endmodule

module SRAM (
  input  nCS,
  input  nWE,
  input  nOE,
  input  [10:0] Addr,
  input  [7:0] Data_In,
  output [7:0] Data_Out
);

  wire not_1_out, not_2_out, not_3_out;

  not not_1 (not_1_out, nCS);
  not not_2 (not_2_out, nWE);
  not not_3 (not_3_out, nOE);
  RAM #(.addrWidth(11), .bus("separate")) ram_1 (
    .addr(Addr), .din(Data_In), .data(Data_Out), .str(not_2_out), .sel(not_1_out), .clk(not_1_out),
    .ld(not_3_out));  // open: clr
endmodule

module LS373 (
  input  LE,
  input  nOE,
  input  [7:0] val_in,
  output [7:0] val_out
);

  wire not_1_out;
  wire [7:0] register_1_q;

  not not_1 (not_1_out, nOE);
  Register #(.trigger("high")) register_1 (.D(val_in), .en(LE), .Q(register_1_q), .clk(LE));  // open: clr
  assign val_out = not_1_out ? register_1_q : 8'bz;  // Controlled_Buffer controlled_buffer_1
endmodule

module NROM_Cartridge (
  input  [7:0] PPUData_In,
  input  nRD,
  input  nWR,
  input  [13:0] PPUAddr,
  input  nPA13,
  input  V_Mirroring,
  output [7:0] PPUData_Out,
  output nVRAM_CS,
  output VRAM_A10
);

  wire nor_1_out;

  nor nor_1 (nor_1_out, nRD, PPUAddr[13]);
  ROM #(.addrWidth(13)) rom_1 (.addr(PPUAddr[12:0]), .data(PPUData_Out), .sel(nor_1_out));
  Multiplexer #(.enable("false")) multiplexer_1 (
    .in0(PPUAddr[11]), .in1(PPUAddr[10]), .out(VRAM_A10), .sel(V_Mirroring));

  assign nVRAM_CS = nPA13;

  // Notes on the sheet:
  //   N.C.
  //   N.C.
  //   1: V-Mirroring, 0: H-Mirroring
  //   Simple NROM cartridge (without PRG)
  //   CHR-ROM (0x2000 bytes)
endmodule

module VideoDumper (
  input  CLK,
  input  [10:0] VideoIn
);
endmodule
